# Fritzing sketch assignment1 (saved by Fritzing 0.9.3b)
breadboards: 1

parts:
  Part1 = Arduino Uno (Rev3)
  J1 = Piezo Speaker
  LED1 = LED - 5mm [color="Green (565nm)" package="5 mm [THT]"]
  LED2 = LED - 5mm [color="Red (633nm)" package="5 mm [THT]"]
  R1 = Resistor [tolerance=±5% resistance=220 package=THT]
  R2 = Resistor [tolerance=±5% resistance=220 package=THT]
  R3 = Resistor [tolerance=±5% resistance=220 package=THT]
  S1 = Magnetic Door Switch [package=reed_switch_plastic]

nets:
  N1: Part1.D9_PWM, LED2.cathode
  N2: Part1.D10_PWM/SS, LED1.cathode
  N3: Part1.D3_PWM, J1.pin2
  N4: Part1.D4, S1.2
  N5: J1.pin1, R3.Pin_1
  N6: LED1.anode, R1.Pin_0
  N7: LED2.anode, R2.Pin_0
  N8: R1.Pin_1, R2.Pin_1, R3.Pin_0, S1.1
