# Fritzing sketch Oppgave3M2M (saved by Fritzing 0.9.3b)
breadboards: 1

parts:
  Part1 = Photon
  S1 = Magnetic Door Switch [package=reed_switch_plastic]
  PIR1 = PIR sensor
  LED1 = LED - 5mm [color="Red (633nm)" package="5 mm [THT]"]
  R1 = Resistor [tolerance=±5% resistance=220 package=THT]

nets:
  GND: Part1.GND, S1.2, PIR1.GND, LED1.cathode
  VIN: Part1.VIN, PIR1.VDD
  N1: Part1.D0, PIR1.SIG
  N2: Part1.D1, R1.Pin_0
  N3: Part1.D3, S1.1
  N4: LED1.anode, R1.Pin_1
